// Logisim project Lab_2.circ as structural Verilog: 1 circuit, main circuit main
module main (
  input  in_1,
  input  in_2,
  input  in_3,
  input  in_4,
  input  in_5,
  input  in_6,
  input  in_7,
  input  in_8,
  input  in_9,
  output out_10,
  output out_11,
  output out_12,
  output out_13,
  output out_14,
  output out_15,
  output out_16
);

  wire and_1_out, or_1_out;

  or or_1 (or_1_out, in_2, in_3);
  nor nor_1 (out_12, in_2, in_3);
  not not_1 (out_11, or_1_out);
  and and_1 (and_1_out, in_8, in_9);
  nand nand_1 (out_16, in_8, in_9);
  not not_2 (out_15, and_1_out);
  not not_3 (out_10, in_1);
  and and_2 (out_13, in_4, in_5);
  or or_2 (out_14, in_6, in_7);

  // Notes on the sheet:
  //   NOR Gate
  //   NAND Gate
  //   NOT Gate
  //   AND Gate
  //   OR Gate
endmodule
