// Logisim project MUL.circ as structural Verilog: 1 circuit, main circuit main
module main (
  input  a,
  input  b,
  input  A_2,
  input  B_2,
  input  C,
  input  D,
  output out_7
);

  wire and_1_out, and_2_out, and_3_out, and_4_out, not_1_out, not_2_out;

  not not_1 (not_1_out, a);
  not not_2 (not_2_out, b);
  and and_1 (and_1_out, A_2, not_2_out, not_1_out);
  and and_2 (and_2_out, B_2, not_2_out, a);
  and and_3 (and_3_out, C, b, not_1_out);
  and and_4 (and_4_out, D, b, a);
  or or_1 (out_7, and_1_out, and_2_out, and_3_out, and_4_out);

  // Notes on the sheet:
  //   NOT GATE
  //   AND GATE
  //   OR GATE
endmodule
