// Logisim project Mux.circ as structural Verilog: 1 circuit, main circuit main
module main (
  input  I,
  input  a,
  input  S1,
  input  b,
  input  S0,
  input  A_2,
  input  B_2,
  input  C,
  input  D,
  output D3,
  output D2,
  output out_12,
  output D1,
  output D0
);

  wire and_5_out, and_6_out, and_7_out, and_8_out, not_1_out, not_2_out, not_3_out, not_4_out;

  not not_1 (not_1_out, S1);
  not not_2 (not_2_out, S0);
  and and_1 (D3, S1, S0, I);
  and and_2 (D2, not_1_out, S0, I);
  and and_3 (D1, S1, not_2_out, I);
  and and_4 (D0, not_1_out, not_2_out, I);
  not not_3 (not_3_out, a);
  not not_4 (not_4_out, b);
  and and_5 (and_5_out, A_2, not_4_out, not_3_out);
  and and_6 (and_6_out, B_2, not_4_out, a);
  and and_7 (and_7_out, C, b, not_3_out);
  and and_8 (and_8_out, D, b, a);
  or or_1 (out_12, and_5_out, and_6_out, and_7_out, and_8_out);

  // Notes on the sheet:
  //   De Multiplexer
  //   Multiplexer
endmodule
