// Logisim project demux.circ as structural Verilog: 1 circuit, main circuit main
module main (
  input  S1,
  input  S0,
  input  D,
  output Y0,
  output Y1,
  output Y2,
  output Y3
);

  wire not_1_out, not_2_out;

  not not_1 (not_1_out, S1);
  not not_2 (not_2_out, S0);
  and and_1 (Y0, not_1_out, D, not_2_out);
  and and_2 (Y1, not_1_out, D, S0);
  and and_3 (Y2, S1, D, not_2_out);
  and and_4 (Y3, S0, D, S1);
endmodule
